// Logisim project phase1.3.circ as structural Verilog
module main (
);

  wire alu_1_branch, ALUsrc, clock_1_out, JALR, MemRead, MemToReg, MemWrite, RegW, SSET, ZeroExtend;
  wire [1:0] PCSrc;
  wire [4:0] instruction_memory_1_out_4, instruction_memory_1_out_5, instruction_memory_1_out_6,
       multiplexer_1_out, undriven;
  wire [5:0] instruction_memory_1_out_7;
  wire [10:0] instruction_memory_1_out_2;
  wire [11:0] alucontrol_1_aluop;
  wire [19:0] pc_1_pc20;
  wire [31:0] alu_1_result, data_memory_1_out_6, extendunit_1_out_3, multiplexer_2_out, multiplexer_3_out,
       multiplexer_4_out, multiplexer_5_out, pc_1_nextpc32, regfile_1_busa, regfile_1_busb, shifter_1_out;

  PC pc_1 (
    .ImmL5(undriven), .JALRPC(alu_1_result[19:0]), .Branch(alu_1_branch), .PCSrc(PCSrc), .Clock(clock_1_out),
    .ImmU11(instruction_memory_1_out_2), .NextPC32(pc_1_nextpc32), .PC20(pc_1_pc20));
  Clock clock_1 (.out(clock_1_out));
  instruction_memory instruction_memory_1 (
    .in_1(pc_1_pc20), .out_2(instruction_memory_1_out_2[10:5]), .out_3(instruction_memory_1_out_2[4:0]),
    .out_4(instruction_memory_1_out_4), .out_5(instruction_memory_1_out_5),
    .out_6(instruction_memory_1_out_6), .out_7(instruction_memory_1_out_7));
  ControlUnit controlunit_1 (
    .opcode(instruction_memory_1_out_7), .MemWrite(MemWrite), .MemRead(MemRead), .ALUsrc(ALUsrc),
    .RegW(RegW), .JALR(JALR), .SSET(SSET), .PCSrc(PCSrc), .ZeroExtend(ZeroExtend), .MemtoReg(MemToReg));
  ALUcontrol alucontrol_1 (
    .func({instruction_memory_1_out_2[4:0], instruction_memory_1_out_2[10:5]}),
    .OPcode(instruction_memory_1_out_7), .ALUop(alucontrol_1_aluop));
  Multiplexer #(.enable("true"), .width(5)) multiplexer_1 (
    .in0(instruction_memory_1_out_5), .in1(undriven), .out(multiplexer_1_out), .sel(SSET));  // open: en
  ExtendUnit extendunit_1 (
    .in_2({instruction_memory_1_out_2, instruction_memory_1_out_4}), .ExtendOp(ZeroExtend),
    .out_3(extendunit_1_out_3));
  Multiplexer #(.enable("true"), .width(32)) multiplexer_2 (
    .in0(multiplexer_5_out), .in1(pc_1_nextpc32), .out(multiplexer_2_out), .sel(JALR));  // open: en
  regFile regfile_1 (
    .RegWrite(RegW), .clock(clock_1_out), .RA(multiplexer_1_out), .Busw(multiplexer_2_out),
    .RB(instruction_memory_1_out_4), .RW(instruction_memory_1_out_6), .BusA(regfile_1_busa),
    .BusB(regfile_1_busb));  // open: out_12, out_13, out_14, out_15, out_16, out_17, out_18, out_19, out_20, out_21, out_22, out_23, out_24, out_25, out_26, out_27, out_28, out_29, out_30, out_31, out_32, out_33, out_34, out_35, out_36, out_37, out_38, out_7, out_8, out_9, out_10, out_11
  Shifter #(.width(32)) shifter_1 (.in(regfile_1_busa), .\dist (5'b10000), .out(shifter_1_out));
  Multiplexer #(.enable("true"), .width(32)) multiplexer_3 (
    .in0(regfile_1_busa), .in1(shifter_1_out), .out(multiplexer_3_out), .sel(SSET));  // open: en
  ALU alu_1 (
    .ALUop(alucontrol_1_aluop), .A(multiplexer_3_out), .B(multiplexer_4_out), .Result(alu_1_result),
    .Branch(alu_1_branch));
  Multiplexer #(.enable("true"), .width(32)) multiplexer_4 (
    .in0(regfile_1_busb), .in1(extendunit_1_out_3), .out(multiplexer_4_out), .sel(ALUsrc));  // open: en
  data_memory data_memory_1 (
    .in_1(alu_1_result[19:0]), .in_2(regfile_1_busb), .in_3(MemWrite), .in_4(MemRead), .in_5(clock_1_out),
    .out_6(data_memory_1_out_6));
  Multiplexer #(.enable("true"), .width(32)) multiplexer_5 (
    .in0(alu_1_result), .in1(data_memory_1_out_6), .out(multiplexer_5_out), .sel(MemToReg));  // open: en
endmodule

module ALU (
  input  [31:0] A,
  input  [31:0] B,
  input  [11:0] ALUop,
  output [31:0] Result,
  output Branch
);

  wire comparator_1_eq, comparator_1_lt, comparator_2_lt, multiplexer_4_out, not_3_out, not_4_out, not_5_out;
  wire [31:0] adder_1_out, and_1_out, bit_extender_1_out, multiplexer_1_out, multiplexer_2_out,
       multiplexer_3_out, multiplier_1_out, not_1_out, not_2_out, or_1_out, shifter_1_out, shifter_2_out,
       shifter_3_out, shifter_4_out, xor_1_out;

  assign not_1_out = ~A;  // NOT_Gate not_1, 32 bits wide
  assign not_2_out = ~B;  // NOT_Gate not_2, 32 bits wide
  Multiplexer #(.enable("true"), .width(32)) multiplexer_1 (
    .in0(A), .in1(not_1_out), .out(multiplexer_1_out), .sel(ALUop[0]));  // open: en
  Multiplexer #(.enable("true"), .width(32)) multiplexer_2 (
    .in0(B), .in1(not_2_out), .out(multiplexer_2_out), .sel(ALUop[1]));  // open: en
  Shifter #(.width(32)) shifter_1 (.in(multiplexer_1_out), .\dist (multiplexer_2_out[4:0]), .out(shifter_1_out));
  Shifter #(.shift("lr"), .width(32)) shifter_2 (
    .in(multiplexer_1_out), .\dist (multiplexer_2_out[4:0]), .out(shifter_2_out));
  Shifter #(.shift("ar"), .width(32)) shifter_3 (
    .in(multiplexer_1_out), .\dist (multiplexer_2_out[4:0]), .out(shifter_3_out));
  Shifter #(.shift("rr"), .width(32)) shifter_4 (
    .in(multiplexer_1_out), .\dist (multiplexer_2_out[4:0]), .out(shifter_4_out));
  assign xor_1_out = multiplexer_1_out ^ multiplexer_2_out;  // XOR_Gate xor_1, 32 bits wide
  assign or_1_out = multiplexer_1_out | multiplexer_2_out;  // OR_Gate or_1, 32 bits wide
  assign and_1_out = multiplexer_1_out & multiplexer_2_out;  // AND_Gate and_1, 32 bits wide
  Multiplier #(.width(32)) multiplier_1 (
    .a(multiplexer_1_out), .b(multiplexer_2_out), .out(multiplier_1_out));  // open: cin, cout
  Adder #(.width(32)) adder_1 (
    .a(multiplexer_1_out), .b(multiplexer_2_out), .out(adder_1_out), .cin(ALUop[1]));  // open: cout
  Comparator #(.width(32)) comparator_1 (.a(A), .b(B), .eq(comparator_1_eq), .lt(comparator_1_lt));  // open: gt
  Comparator #(.mode("unsigned"), .width(32)) comparator_2 (.a(A), .b(B), .lt(comparator_2_lt));  // open: gt, eq
  not not_3 (not_3_out, comparator_1_lt);
  not not_4 (not_4_out, comparator_1_eq);
  not not_5 (not_5_out, comparator_2_lt);
  Multiplexer #(.enable("true"), .select(2), .width(32)) multiplexer_3 (
    .in0(shifter_1_out), .in1(shifter_2_out), .in2(shifter_3_out), .in3(shifter_4_out),
    .out(multiplexer_3_out), .sel(ALUop[3:2]));  // open: en
  assign bit_extender_1_out = {{31{1'b0}}, multiplexer_4_out};  // Bit_Extender bit_extender_1
  Multiplexer #(.enable("true"), .select(2)) multiplexer_4 (
    .in0(comparator_1_eq), .in1(comparator_1_lt), .in2(comparator_2_lt), .out(multiplexer_4_out),
    .sel(ALUop[5:4]));  // open: in3, en
  Multiplexer #(.enable("true"), .select(3)) multiplexer_5 (
    .in0(1'b0), .in1(comparator_1_lt), .in2(not_3_out), .in3(comparator_1_eq), .in4(not_4_out),
    .in5(comparator_2_lt), .in6(not_5_out), .out(Branch), .sel(ALUop[8:6]));  // open: in7, en
  Multiplexer #(.enable("true"), .select(3), .width(32)) multiplexer_6 (
    .in0(multiplexer_3_out), .in1(adder_1_out), .in2(bit_extender_1_out), .in3(xor_1_out), .in4(or_1_out),
    .in5(and_1_out), .in6(multiplier_1_out), .out(Result), .sel(ALUop[11:9]));  // open: in7, en

  // Other names for the same wires on the sheet: Ainvert = ALUop[0]; Binvert = ALUop[1]; ShiftOp[1:0] = ALUop[3:2];
  //   SetOp[1:0] = ALUop[5:4]; BranchOp[2:0] = ALUop[8:6]; ALUop_t[2:0] = ALUop[11:9]
endmodule

module PC (
  input  Branch,
  input  [19:0] JALRPC,
  input  [10:0] ImmU11,
  input  Clock,
  input  [4:0] ImmL5,
  input  [1:0] PCSrc,
  output [31:0] NextPC32,
  output [19:0] PC20
);

  wire [1:0] multiplexer_2_out;
  wire [19:0] adder_1_out, adder_2_out, bit_extender_1_out, multiplexer_1_out;

  Multiplexer #(.enable("true"), .select(2), .width(20)) multiplexer_1 (
    .in0(adder_1_out), .in1(adder_2_out), .in2(JALRPC), .out(multiplexer_1_out), .sel(multiplexer_2_out));  // open: in3, en
  Multiplexer #(.enable("true"), .width(2)) multiplexer_2 (
    .in0(PCSrc), .in1(2'b01), .out(multiplexer_2_out), .sel(Branch));  // open: en
  Register #(.width(20)) ProgramCounter (.D(multiplexer_1_out), .en(1'b1), .clk(Clock), .Q(PC20));  // open: clr
  Adder #(.width(20)) adder_1 (.a(PC20), .b(20'h1), .out(adder_1_out));  // open: cin, cout
  assign bit_extender_1_out = {{4{ImmL5[4]}}, {ImmL5, ImmU11}};  // Bit_Extender bit_extender_1
  Adder #(.width(20)) adder_2 (.a(adder_1_out), .b(bit_extender_1_out), .out(adder_2_out));  // open: cin, cout
  assign NextPC32 = {{12{adder_1_out[19]}}, adder_1_out};  // Bit_Extender bit_extender_2
endmodule

module instruction_memory (
  input  [19:0] in_1,
  output [5:0] out_2,
  output [4:0] out_3,
  output [4:0] out_4,
  output [4:0] out_5,
  output [4:0] out_6,
  output [5:0] out_7
);

  ROM #(.addrWidth(20), .dataWidth(32)) rom_1 (.addr(in_1), .data({out_7, out_6, out_5, out_4, out_3, out_2}));

  // Notes on the sheet:
  //   contents of rom_1 (hex, n*v repeats v):
  //   0 200000 400000 600000 800000 a00000 c00000 e00000 1000000 1200000 1400000 1600000 1800000 1a00000 1
  //   2 3 4 5 6 7 8 9 a b c d e f 10 11 12 13 14 15 16 17
endmodule

module data_memory (
  input  [19:0] in_1,
  input  [31:0] in_2,
  input  in_3,
  input  in_4,
  input  in_5,
  output [31:0] out_6
);

  RAM #(.addrWidth(20), .dataWidth(32)) ram_1 (.addr(in_1), .we(in_3), .oe(in_4), .clk(in_5), .din(in_2), .dout(out_6));
endmodule

module ControlUnit (
  input  [5:0] opcode,
  output MemtoReg,
  output MemWrite,
  output MemRead,
  output ALUsrc,
  output RegW,
  output JALR,
  output SSET,
  output [1:0] PCSrc,
  output ZeroExtend
);

  wire and_3_out, and_4_out, and_5_out, and_9_out, and_10_out, and_11_out, and_12_out, not_1_out, not_2_out,
       not_3_out, not_4_out, not_5_out;

  not not_1 (not_1_out, opcode[4]);
  not not_2 (not_2_out, opcode[3]);
  not not_3 (not_3_out, opcode[2]);
  not not_4 (not_4_out, opcode[1]);
  not not_5 (not_5_out, opcode[0]);
  and and_1 (MemWrite, opcode[4], not_3_out, not_4_out, opcode[0]);
  and and_2 (MemRead, opcode[4], not_3_out, not_4_out, not_5_out);
  and and_3 (and_3_out, opcode[2], opcode[0]);
  and and_4 (and_4_out, opcode[2], opcode[1]);
  and and_5 (and_5_out, not_3_out, not_4_out, not_5_out);
  and and_6 (JALR, opcode[3], opcode[2], opcode[1], opcode[0]);
  and and_7 (SSET, opcode[3], opcode[2], opcode[1], not_5_out);
  and and_8 (PCSrc[1], opcode[3], opcode[2], opcode[1], opcode[0]);
  and and_9 (and_9_out, not_1_out, not_2_out, opcode[1], opcode[0]);
  and and_10 (and_10_out, opcode[3], opcode[2], not_5_out);
  and and_11 (and_11_out, not_1_out, not_3_out, opcode[0]);
  and and_12 (and_12_out, not_1_out, not_3_out, opcode[1]);
  or or_1 (ALUsrc, and_3_out, and_4_out, opcode[3], opcode[4]);
  or or_2 (RegW, not_1_out, and_5_out);
  or or_3 (ZeroExtend, and_9_out, and_10_out, and_11_out, and_12_out);

  assign MemtoReg = opcode[4];
  assign PCSrc[0] = 1'b0;
endmodule

module ExtendUnit (
  input  ExtendOp,
  input  [15:0] in_2,
  output [31:0] out_3
);

  wire [31:0] bit_extender_1_out, bit_extender_2_out;

  assign bit_extender_1_out = {{16{in_2[15]}}, in_2};  // Bit_Extender bit_extender_1
  Multiplexer #(.enable("true"), .width(32)) multiplexer_1 (
    .in0(bit_extender_1_out), .in1(bit_extender_2_out), .out(out_3), .sel(ExtendOp));  // open: en
  assign bit_extender_2_out = {{16{1'b0}}, in_2};  // Bit_Extender bit_extender_2
endmodule

module ALUcontrol (
  input  [10:0] func,
  input  [5:0] OPcode,
  output [11:0] ALUop
);

  wire and_2_out, and_3_out, and_4_out, and_5_out, and_6_out, and_7_out, and_8_out, and_9_out, and_10_out,
       and_11_out, and_14_out, and_15_out, and_16_out, and_17_out, and_18_out, and_19_out, and_20_out,
       and_21_out, and_22_out, and_23_out, and_24_out, and_25_out, and_26_out, and_27_out, not_2_out,
       not_3_out, not_4_out, not_6_out, not_7_out, S;
  wire [11:0] FuncOut, OpCodeOut;

  not not_1 (FuncOut[4], func[3]);
  not not_2 (not_2_out, func[2]);
  not not_3 (not_3_out, func[1]);
  not not_4 (not_4_out, func[0]);
  and and_1 (FuncOut[0], func[3], func[2], not_4_out);
  and and_2 (and_2_out, FuncOut[4], func[2], not_3_out, func[0]);
  and and_3 (and_3_out, func[3], func[2], not_4_out);
  and and_4 (and_4_out, func[3], func[1]);
  and and_5 (and_5_out, func[3], func[2]);
  and and_6 (and_6_out, func[2], func[1]);
  and and_7 (and_7_out, func[3], not_2_out, not_3_out);
  and and_8 (and_8_out, func[3], not_3_out, func[0]);
  and and_9 (and_9_out, FuncOut[4], func[2], not_3_out);
  and and_10 (and_10_out, func[3], not_2_out, func[0]);
  and and_11 (and_11_out, func[2], not_3_out, not_4_out);
  or or_1 (FuncOut[1], and_2_out, and_3_out);
  or or_2 (FuncOut[11], and_4_out, and_5_out);
  or or_3 (FuncOut[10], and_6_out, and_7_out, and_8_out);
  or or_4 (FuncOut[9], and_9_out, and_10_out, and_11_out);
  or or_5 (S, OPcode[0], OPcode[1], OPcode[2], OPcode[3], OPcode[4], OPcode[5]);
  not not_5 (OpCodeOut[4], OPcode[3]);
  not not_6 (not_6_out, OPcode[2]);
  not not_7 (not_7_out, OPcode[1]);
  not not_8 (OpCodeOut[2], OPcode[0]);
  Multiplexer #(.enable("true"), .width(12)) multiplexer_1 (
    .in0({FuncOut[11:9], 3'b000, func[0], FuncOut[4], func[1:0], FuncOut[1:0]}),
    .in1({OpCodeOut[11:6], OPcode[0], OpCodeOut[4:0]}), .out(ALUop), .sel(S));  // open: en
  and and_12 (OpCodeOut[0], OPcode[3], OPcode[2], not_7_out, OpCodeOut[2]);
  and and_13 (OpCodeOut[1], OPcode[3], OPcode[2], not_7_out, OpCodeOut[2]);
  and and_14 (and_14_out, OPcode[1], OPcode[0]);
  and and_15 (and_15_out, OPcode[4], OPcode[1], OPcode[0]);
  and and_16 (and_16_out, OPcode[4], OPcode[2], OPcode[1]);
  and and_17 (and_17_out, OPcode[4], not_6_out, OPcode[1], OpCodeOut[2]);
  and and_18 (and_18_out, OPcode[4], OPcode[2], OPcode[0]);
  and and_19 (and_19_out, OPcode[4], OPcode[1], OpCodeOut[2]);
  and and_20 (and_20_out, OPcode[4], OPcode[2], OpCodeOut[2]);
  and and_21 (and_21_out, OPcode[3], not_6_out, OPcode[1]);
  and and_22 (and_22_out, OPcode[3], OPcode[2], not_7_out, OpCodeOut[2]);
  and and_23 (and_23_out, OpCodeOut[4], OPcode[2], OPcode[1]);
  and and_24 (and_24_out, OPcode[3], not_6_out, not_7_out);
  and and_25 (and_25_out, OPcode[2], not_7_out, OPcode[0]);
  and and_26 (and_26_out, OPcode[3], OPcode[0]);
  and and_27 (and_27_out, OPcode[3], OPcode[2]);
  or or_6 (OpCodeOut[3], and_14_out, OPcode[2]);
  or or_7 (OpCodeOut[8], and_15_out, and_16_out);
  or or_8 (OpCodeOut[7], and_17_out, and_18_out);
  or or_9 (OpCodeOut[6], and_19_out, and_20_out);
  or or_10 (OpCodeOut[11], and_21_out, and_22_out);
  or or_11 (OpCodeOut[10], and_23_out, and_24_out);
  or or_12 (OpCodeOut[9], and_25_out, and_26_out, and_27_out, OPcode[4]);

  // Other names for the same wires on the sheet: FuncOut (some bits) = {func[0], func[1:0]}; OpCodeOut[5] = OPcode[0]
endmodule

module regFile (
  input  [4:0] RB,
  input  [4:0] RA,
  input  [4:0] RW,
  input  RegWrite,
  input  clock,
  input  [31:0] Busw,
  output [31:0] out_7,
  output [31:0] out_8,
  output [31:0] out_9,
  output [31:0] out_10,
  output [31:0] out_11,
  output [31:0] out_12,
  output [31:0] out_13,
  output [31:0] out_14,
  output [31:0] out_15,
  output [31:0] out_16,
  output [31:0] out_17,
  output [31:0] out_18,
  output [31:0] out_19,
  output [31:0] out_20,
  output [31:0] out_21,
  output [31:0] out_22,
  output [31:0] out_23,
  output [31:0] out_24,
  output [31:0] out_25,
  output [31:0] out_26,
  output [31:0] out_27,
  output [31:0] out_28,
  output [31:0] out_29,
  output [31:0] out_30,
  output [31:0] out_31,
  output [31:0] out_32,
  output [31:0] out_33,
  output [31:0] out_34,
  output [31:0] out_35,
  output [31:0] out_36,
  output [31:0] out_37,
  output [31:0] out_38,
  output [31:0] BusB,
  output [31:0] BusA
);

  wire and_1_out, and_2_out, and_3_out, and_4_out, and_5_out, and_6_out, and_7_out, and_8_out, and_9_out,
       and_10_out, and_11_out, and_12_out, and_13_out, and_14_out, and_15_out, and_16_out, and_17_out,
       and_18_out, and_19_out, and_20_out, and_21_out, and_22_out, and_23_out, and_24_out, and_25_out,
       and_26_out, and_27_out, and_28_out, and_29_out, and_30_out, and_31_out, decoder_1_out1,
       decoder_1_out2, decoder_1_out3, decoder_1_out4, decoder_1_out5, decoder_1_out6, decoder_1_out7,
       decoder_1_out8, decoder_1_out9, decoder_1_out10, decoder_1_out11, decoder_1_out12, decoder_1_out13,
       decoder_1_out14, decoder_1_out15, decoder_1_out16, decoder_1_out17, decoder_1_out18, decoder_1_out19,
       decoder_1_out20, decoder_1_out21, decoder_1_out22, decoder_1_out23, decoder_1_out24, decoder_1_out25,
       decoder_1_out26, decoder_1_out27, decoder_1_out28, decoder_1_out29, decoder_1_out30, decoder_1_out31,
       decoder_2_out0, decoder_2_out1, decoder_2_out2, decoder_2_out3, decoder_2_out4, decoder_2_out5,
       decoder_2_out6, decoder_2_out7, decoder_2_out8, decoder_2_out9, decoder_2_out10, decoder_2_out11,
       decoder_2_out12, decoder_2_out13, decoder_2_out14, decoder_2_out15, decoder_2_out16, decoder_2_out17,
       decoder_2_out18, decoder_2_out19, decoder_2_out20, decoder_2_out21, decoder_2_out22, decoder_2_out23,
       decoder_2_out24, decoder_2_out25, decoder_2_out26, decoder_2_out27, decoder_2_out28, decoder_2_out29,
       decoder_2_out30, decoder_2_out31, decoder_3_out0, decoder_3_out1, decoder_3_out2, decoder_3_out3,
       decoder_3_out4, decoder_3_out5, decoder_3_out6, decoder_3_out7, decoder_3_out8, decoder_3_out9,
       decoder_3_out10, decoder_3_out11, decoder_3_out12, decoder_3_out13, decoder_3_out14, decoder_3_out15,
       decoder_3_out16, decoder_3_out17, decoder_3_out18, decoder_3_out19, decoder_3_out20, decoder_3_out21,
       decoder_3_out22, decoder_3_out23, decoder_3_out24, decoder_3_out25, decoder_3_out26, decoder_3_out27,
       decoder_3_out28, decoder_3_out29, decoder_3_out30, decoder_3_out31;
  wire [31:0] controlled_buffer_1_out, controlled_buffer_33_out, undriven;

  Decoder #(.enable("false"), .select(5)) decoder_1 (
    .out1(decoder_1_out1), .out2(decoder_1_out2), .out3(decoder_1_out3), .out4(decoder_1_out4),
    .out5(decoder_1_out5), .out6(decoder_1_out6), .out7(decoder_1_out7), .out8(decoder_1_out8),
    .out9(decoder_1_out9), .out10(decoder_1_out10), .out11(decoder_1_out11), .out12(decoder_1_out12),
    .out13(decoder_1_out13), .out14(decoder_1_out14), .out15(decoder_1_out15), .out16(decoder_1_out16),
    .out17(decoder_1_out17), .out18(decoder_1_out18), .out19(decoder_1_out19), .out20(decoder_1_out20),
    .out21(decoder_1_out21), .out22(decoder_1_out22), .out23(decoder_1_out23), .out24(decoder_1_out24),
    .out25(decoder_1_out25), .out26(decoder_1_out26), .out27(decoder_1_out27), .out28(decoder_1_out28),
    .out29(decoder_1_out29), .out30(decoder_1_out30), .out31(decoder_1_out31), .sel(RW));  // open: out0
  Register #(.width(32)) register_1 (.D(undriven), .en(and_1_out), .clk(clock), .Q(out_8));  // open: clr
  and and_1 (and_1_out, decoder_1_out1, RegWrite);
  Register #(.width(32)) register_2 (.D(undriven), .en(and_2_out), .clk(clock), .Q(out_9));  // open: clr
  and and_2 (and_2_out, decoder_1_out2, RegWrite);
  Register #(.width(32)) register_3 (.D(undriven), .en(and_3_out), .clk(clock), .Q(out_10));  // open: clr
  and and_3 (and_3_out, decoder_1_out3, RegWrite);
  Register #(.width(32)) register_4 (.D(undriven), .en(and_4_out), .clk(clock), .Q(out_11));  // open: clr
  and and_4 (and_4_out, decoder_1_out4, RegWrite);
  Register #(.width(32)) register_5 (.D(undriven), .en(and_5_out), .clk(clock), .Q(out_12));  // open: clr
  and and_5 (and_5_out, decoder_1_out5, RegWrite);
  Register #(.width(32)) register_6 (.D(undriven), .en(and_6_out), .clk(clock), .Q(out_13));  // open: clr
  and and_6 (and_6_out, decoder_1_out6, RegWrite);
  Register #(.width(32)) register_7 (.D(undriven), .en(and_7_out), .clk(clock), .Q(out_14));  // open: clr
  and and_7 (and_7_out, decoder_1_out7, RegWrite);
  Register #(.width(32)) register_8 (.D(undriven), .en(and_8_out), .clk(clock), .Q(out_15));  // open: clr
  and and_8 (and_8_out, decoder_1_out8, RegWrite);
  Register #(.width(32)) register_9 (.D(undriven), .en(and_9_out), .clk(clock), .Q(out_16));  // open: clr
  and and_9 (and_9_out, decoder_1_out9, RegWrite);
  Register #(.width(32)) register_10 (.D(undriven), .en(and_10_out), .clk(clock), .Q(out_17));  // open: clr
  and and_10 (and_10_out, decoder_1_out10, RegWrite);
  Register #(.width(32)) register_11 (.D(undriven), .en(and_11_out), .clk(clock), .Q(out_18));  // open: clr
  and and_11 (and_11_out, decoder_1_out11, RegWrite);
  Register #(.width(32)) register_12 (.D(undriven), .en(and_12_out), .clk(clock), .Q(out_19));  // open: clr
  and and_12 (and_12_out, decoder_1_out12, RegWrite);
  Register #(.width(32)) register_13 (.D(undriven), .en(and_13_out), .clk(clock), .Q(out_20));  // open: clr
  and and_13 (and_13_out, decoder_1_out13, RegWrite);
  Register #(.width(32)) register_14 (.D(undriven), .en(and_14_out), .clk(clock), .Q(out_21));  // open: clr
  and and_14 (and_14_out, decoder_1_out14, RegWrite);
  Register #(.width(32)) register_15 (.D(undriven), .en(and_15_out), .clk(clock), .Q(out_22));  // open: clr
  and and_15 (and_15_out, decoder_1_out15, RegWrite);
  Register #(.width(32)) register_16 (.D(undriven), .en(and_16_out), .clk(clock), .Q(out_23));  // open: clr
  and and_16 (and_16_out, decoder_1_out16, RegWrite);
  Register #(.width(32)) register_17 (.D(undriven), .en(and_17_out), .clk(clock), .Q(out_24));  // open: clr
  and and_17 (and_17_out, decoder_1_out17, RegWrite);
  Register #(.width(32)) register_18 (.D(undriven), .en(and_18_out), .clk(clock), .Q(out_25));  // open: clr
  and and_18 (and_18_out, decoder_1_out18, RegWrite);
  Register #(.width(32)) register_19 (.D(undriven), .en(and_19_out), .clk(clock), .Q(out_26));  // open: clr
  and and_19 (and_19_out, decoder_1_out19, RegWrite);
  Register #(.width(32)) register_20 (.D(undriven), .en(and_20_out), .clk(clock), .Q(out_27));  // open: clr
  and and_20 (and_20_out, decoder_1_out20, RegWrite);
  Register #(.width(32)) register_21 (.D(undriven), .en(and_21_out), .clk(clock), .Q(out_28));  // open: clr
  and and_21 (and_21_out, decoder_1_out21, RegWrite);
  Register #(.width(32)) register_22 (.D(undriven), .en(and_22_out), .clk(clock), .Q(out_29));  // open: clr
  and and_22 (and_22_out, decoder_1_out22, RegWrite);
  Register #(.width(32)) register_23 (.D(undriven), .en(and_23_out), .clk(clock), .Q(out_30));  // open: clr
  and and_23 (and_23_out, decoder_1_out23, RegWrite);
  Register #(.width(32)) register_24 (.D(undriven), .en(and_24_out), .clk(clock), .Q(out_31));  // open: clr
  and and_24 (and_24_out, decoder_1_out24, RegWrite);
  Register #(.width(32)) register_25 (.D(undriven), .en(and_25_out), .clk(clock), .Q(out_32));  // open: clr
  and and_25 (and_25_out, decoder_1_out25, RegWrite);
  Register #(.width(32)) register_26 (.D(undriven), .en(and_26_out), .clk(clock), .Q(out_33));  // open: clr
  and and_26 (and_26_out, decoder_1_out26, RegWrite);
  Register #(.width(32)) register_27 (.D(undriven), .en(and_27_out), .clk(clock), .Q(out_34));  // open: clr
  and and_27 (and_27_out, decoder_1_out27, RegWrite);
  Register #(.width(32)) register_28 (.D(undriven), .en(and_28_out), .clk(clock), .Q(out_35));  // open: clr
  and and_28 (and_28_out, decoder_1_out28, RegWrite);
  Register #(.width(32)) register_29 (.D(undriven), .en(and_29_out), .clk(clock), .Q(out_36));  // open: clr
  and and_29 (and_29_out, decoder_1_out29, RegWrite);
  Register #(.width(32)) register_30 (.D(undriven), .en(and_30_out), .clk(clock), .Q(out_37));  // open: clr
  and and_30 (and_30_out, decoder_1_out30, RegWrite);
  Register #(.width(32)) register_31 (.D(undriven), .en(and_31_out), .clk(clock), .Q(out_38));  // open: clr
  and and_31 (and_31_out, decoder_1_out31, RegWrite);
  Decoder #(.enable("false"), .select(5)) decoder_2 (
    .out0(decoder_2_out0), .out1(decoder_2_out1), .out2(decoder_2_out2), .out3(decoder_2_out3),
    .out4(decoder_2_out4), .out5(decoder_2_out5), .out6(decoder_2_out6), .out7(decoder_2_out7),
    .out8(decoder_2_out8), .out9(decoder_2_out9), .out10(decoder_2_out10), .out11(decoder_2_out11),
    .out12(decoder_2_out12), .out13(decoder_2_out13), .out14(decoder_2_out14), .out15(decoder_2_out15),
    .out16(decoder_2_out16), .out17(decoder_2_out17), .out18(decoder_2_out18), .out19(decoder_2_out19),
    .out20(decoder_2_out20), .out21(decoder_2_out21), .out22(decoder_2_out22), .out23(decoder_2_out23),
    .out24(decoder_2_out24), .out25(decoder_2_out25), .out26(decoder_2_out26), .out27(decoder_2_out27),
    .out28(decoder_2_out28), .out29(decoder_2_out29), .out30(decoder_2_out30), .out31(decoder_2_out31),
    .sel(RA));
  assign controlled_buffer_1_out = decoder_2_out2 ? out_9 : 32'bz;  // Controlled_Buffer controlled_buffer_1
  assign controlled_buffer_1_out = decoder_2_out3 ? out_10 : 32'bz;  // Controlled_Buffer controlled_buffer_2
  assign controlled_buffer_1_out = decoder_2_out4 ? out_11 : 32'bz;  // Controlled_Buffer controlled_buffer_3
  assign controlled_buffer_1_out = decoder_2_out5 ? out_12 : 32'bz;  // Controlled_Buffer controlled_buffer_4
  assign controlled_buffer_1_out = decoder_2_out6 ? out_13 : 32'bz;  // Controlled_Buffer controlled_buffer_5
  assign controlled_buffer_1_out = decoder_2_out7 ? out_14 : 32'bz;  // Controlled_Buffer controlled_buffer_6
  assign controlled_buffer_1_out = decoder_2_out8 ? out_15 : 32'bz;  // Controlled_Buffer controlled_buffer_7
  assign controlled_buffer_1_out = decoder_2_out9 ? out_16 : 32'bz;  // Controlled_Buffer controlled_buffer_8
  assign controlled_buffer_1_out = decoder_2_out10 ? out_17 : 32'bz;  // Controlled_Buffer controlled_buffer_9
  assign controlled_buffer_1_out = decoder_2_out11 ? out_18 : 32'bz;  // Controlled_Buffer controlled_buffer_10
  assign controlled_buffer_1_out = decoder_2_out12 ? out_19 : 32'bz;  // Controlled_Buffer controlled_buffer_11
  assign controlled_buffer_1_out = decoder_2_out13 ? out_20 : 32'bz;  // Controlled_Buffer controlled_buffer_12
  assign controlled_buffer_1_out = decoder_2_out14 ? out_21 : 32'bz;  // Controlled_Buffer controlled_buffer_13
  assign controlled_buffer_1_out = decoder_2_out15 ? out_22 : 32'bz;  // Controlled_Buffer controlled_buffer_14
  assign controlled_buffer_1_out = decoder_2_out16 ? out_23 : 32'bz;  // Controlled_Buffer controlled_buffer_15
  assign controlled_buffer_1_out = decoder_2_out17 ? out_24 : 32'bz;  // Controlled_Buffer controlled_buffer_16
  assign controlled_buffer_1_out = decoder_2_out18 ? out_25 : 32'bz;  // Controlled_Buffer controlled_buffer_17
  assign controlled_buffer_1_out = decoder_2_out19 ? out_26 : 32'bz;  // Controlled_Buffer controlled_buffer_18
  assign controlled_buffer_1_out = decoder_2_out20 ? out_27 : 32'bz;  // Controlled_Buffer controlled_buffer_19
  assign controlled_buffer_1_out = decoder_2_out21 ? out_28 : 32'bz;  // Controlled_Buffer controlled_buffer_20
  assign controlled_buffer_1_out = decoder_2_out22 ? out_29 : 32'bz;  // Controlled_Buffer controlled_buffer_21
  assign controlled_buffer_1_out = decoder_2_out23 ? out_30 : 32'bz;  // Controlled_Buffer controlled_buffer_22
  assign controlled_buffer_1_out = decoder_2_out24 ? out_31 : 32'bz;  // Controlled_Buffer controlled_buffer_23
  assign controlled_buffer_1_out = decoder_2_out25 ? out_32 : 32'bz;  // Controlled_Buffer controlled_buffer_24
  assign controlled_buffer_1_out = decoder_2_out26 ? out_33 : 32'bz;  // Controlled_Buffer controlled_buffer_25
  assign controlled_buffer_1_out = decoder_2_out27 ? out_34 : 32'bz;  // Controlled_Buffer controlled_buffer_26
  assign controlled_buffer_1_out = decoder_2_out28 ? out_35 : 32'bz;  // Controlled_Buffer controlled_buffer_27
  assign controlled_buffer_1_out = decoder_2_out29 ? out_36 : 32'bz;  // Controlled_Buffer controlled_buffer_28
  assign controlled_buffer_1_out = decoder_2_out30 ? out_37 : 32'bz;  // Controlled_Buffer controlled_buffer_29
  assign controlled_buffer_1_out = decoder_2_out31 ? out_38 : 32'bz;  // Controlled_Buffer controlled_buffer_30
  assign controlled_buffer_1_out = decoder_2_out0 ? {32{1'b0}} : 32'bz;  // Controlled_Buffer controlled_buffer_31
  assign controlled_buffer_1_out = decoder_2_out1 ? out_8 : 32'bz;  // Controlled_Buffer controlled_buffer_32
  Decoder #(.enable("false"), .select(5)) decoder_3 (
    .out0(decoder_3_out0), .out1(decoder_3_out1), .out2(decoder_3_out2), .out3(decoder_3_out3),
    .out4(decoder_3_out4), .out5(decoder_3_out5), .out6(decoder_3_out6), .out7(decoder_3_out7),
    .out8(decoder_3_out8), .out9(decoder_3_out9), .out10(decoder_3_out10), .out11(decoder_3_out11),
    .out12(decoder_3_out12), .out13(decoder_3_out13), .out14(decoder_3_out14), .out15(decoder_3_out15),
    .out16(decoder_3_out16), .out17(decoder_3_out17), .out18(decoder_3_out18), .out19(decoder_3_out19),
    .out20(decoder_3_out20), .out21(decoder_3_out21), .out22(decoder_3_out22), .out23(decoder_3_out23),
    .out24(decoder_3_out24), .out25(decoder_3_out25), .out26(decoder_3_out26), .out27(decoder_3_out27),
    .out28(decoder_3_out28), .out29(decoder_3_out29), .out30(decoder_3_out30), .out31(decoder_3_out31),
    .sel(RB));
  assign controlled_buffer_33_out = decoder_3_out0 ? {32{1'b0}} : 32'bz;  // Controlled_Buffer controlled_buffer_33
  assign controlled_buffer_33_out = decoder_3_out1 ? out_8 : 32'bz;  // Controlled_Buffer controlled_buffer_34
  assign controlled_buffer_33_out = decoder_3_out2 ? out_9 : 32'bz;  // Controlled_Buffer controlled_buffer_35
  assign controlled_buffer_33_out = decoder_3_out3 ? out_10 : 32'bz;  // Controlled_Buffer controlled_buffer_36
  assign controlled_buffer_33_out = decoder_3_out4 ? out_11 : 32'bz;  // Controlled_Buffer controlled_buffer_37
  assign controlled_buffer_33_out = decoder_3_out5 ? out_12 : 32'bz;  // Controlled_Buffer controlled_buffer_38
  assign controlled_buffer_33_out = decoder_3_out6 ? out_13 : 32'bz;  // Controlled_Buffer controlled_buffer_39
  assign controlled_buffer_33_out = decoder_3_out7 ? out_14 : 32'bz;  // Controlled_Buffer controlled_buffer_40
  assign controlled_buffer_33_out = decoder_3_out8 ? out_15 : 32'bz;  // Controlled_Buffer controlled_buffer_41
  assign controlled_buffer_33_out = decoder_3_out9 ? out_16 : 32'bz;  // Controlled_Buffer controlled_buffer_42
  assign controlled_buffer_33_out = decoder_3_out10 ? out_17 : 32'bz;  // Controlled_Buffer controlled_buffer_43
  assign controlled_buffer_33_out = decoder_3_out11 ? out_18 : 32'bz;  // Controlled_Buffer controlled_buffer_44
  assign controlled_buffer_33_out = decoder_3_out12 ? out_19 : 32'bz;  // Controlled_Buffer controlled_buffer_45
  assign controlled_buffer_33_out = decoder_3_out13 ? out_20 : 32'bz;  // Controlled_Buffer controlled_buffer_46
  assign controlled_buffer_33_out = decoder_3_out14 ? out_21 : 32'bz;  // Controlled_Buffer controlled_buffer_47
  assign controlled_buffer_33_out = decoder_3_out15 ? out_22 : 32'bz;  // Controlled_Buffer controlled_buffer_48
  assign controlled_buffer_33_out = decoder_3_out16 ? out_23 : 32'bz;  // Controlled_Buffer controlled_buffer_49
  assign controlled_buffer_33_out = decoder_3_out17 ? out_24 : 32'bz;  // Controlled_Buffer controlled_buffer_50
  assign controlled_buffer_33_out = decoder_3_out18 ? out_25 : 32'bz;  // Controlled_Buffer controlled_buffer_51
  assign controlled_buffer_33_out = decoder_3_out19 ? out_26 : 32'bz;  // Controlled_Buffer controlled_buffer_52
  assign controlled_buffer_33_out = decoder_3_out20 ? out_27 : 32'bz;  // Controlled_Buffer controlled_buffer_53
  assign controlled_buffer_33_out = decoder_3_out21 ? out_28 : 32'bz;  // Controlled_Buffer controlled_buffer_54
  assign controlled_buffer_33_out = decoder_3_out22 ? out_29 : 32'bz;  // Controlled_Buffer controlled_buffer_55
  assign controlled_buffer_33_out = decoder_3_out23 ? out_30 : 32'bz;  // Controlled_Buffer controlled_buffer_56
  assign controlled_buffer_33_out = decoder_3_out24 ? out_31 : 32'bz;  // Controlled_Buffer controlled_buffer_57
  assign controlled_buffer_33_out = decoder_3_out25 ? out_32 : 32'bz;  // Controlled_Buffer controlled_buffer_58
  assign controlled_buffer_33_out = decoder_3_out26 ? out_33 : 32'bz;  // Controlled_Buffer controlled_buffer_59
  assign controlled_buffer_33_out = decoder_3_out27 ? out_34 : 32'bz;  // Controlled_Buffer controlled_buffer_60
  assign controlled_buffer_33_out = decoder_3_out28 ? out_35 : 32'bz;  // Controlled_Buffer controlled_buffer_61
  assign controlled_buffer_33_out = decoder_3_out29 ? out_36 : 32'bz;  // Controlled_Buffer controlled_buffer_62
  assign controlled_buffer_33_out = decoder_3_out30 ? out_37 : 32'bz;  // Controlled_Buffer controlled_buffer_63
  assign controlled_buffer_33_out = decoder_3_out31 ? out_38 : 32'bz;  // Controlled_Buffer controlled_buffer_64

  assign out_7 = {32{1'b0}};

  // Other names for the same wires on the sheet: R1[31:0] = out_8; R2[31:0] = out_9; R3[31:0] = out_10;
  //   R4[31:0] = out_11; R5[31:0] = out_12; R6[31:0] = out_13; R7[31:0] = out_14; R8[31:0] = out_15;
  //   R9[31:0] = out_16; R10[31:0] = out_17; R11[31:0] = out_18; R12[31:0] = out_19; R13[31:0] = out_20;
  //   R14[31:0] = out_21; R15[31:0] = out_22; R16[31:0] = out_23; R17[31:0] = out_24; R18[31:0] = out_25;
  //   R19[31:0] = out_26; R20[31:0] = out_27; R21[31:0] = out_28; R22[31:0] = out_29; R23[31:0] = out_30;
  //   R24[31:0] = out_31; R25[31:0] = out_32; R26[31:0] = out_33; R27[31:0] = out_34; R28[31:0] = out_35;
  //   R29[31:0] = out_36; R30[31:0] = out_37; R31[31:0] = out_38
endmodule
