// Logisim project MIPS_CPU_phase1.circ as structural Verilog: 9 circuits, main circuit main
module main (
  output [31:0] out_1,
  output [31:0] out_2,
  output [31:0] out_3,
  output [31:0] out_4,
  output [31:0] out_5,
  output [31:0] out_6,
  output [31:0] out_7,
  output [31:0] out_8,
  output [31:0] out_9,
  output [31:0] out_10,
  output [31:0] out_11,
  output [31:0] out_12,
  output [31:0] out_13,
  output [31:0] out_14,
  output [31:0] out_15,
  output [31:0] out_16,
  output [31:0] out_17,
  output [31:0] out_18,
  output [31:0] out_19,
  output [31:0] out_20,
  output [31:0] out_21,
  output [31:0] out_22,
  output [19:0] out_23,
  output [31:0] out_24,
  output [31:0] out_25,
  output [31:0] out_26,
  output [31:0] out_27,
  output [31:0] out_28,
  output [31:0] out_29,
  output [31:0] out_30,
  output [31:0] out_31,
  output [31:0] out_32
);

  wire alu_1_branch, ALUsrc, clock_1_out, JALR, MemRead, MemToReg, MemWrite, RegW, SB, SSET, ZeroExtend;
  wire [1:0] PCSrc;
  wire [4:0] instruction_memory_1_rd_imml, instruction_memory_1_rs1, instruction_memory_1_rs2_imm5,
       multiplexer_1_out;
  wire [5:0] instruction_memory_1_opcode;
  wire [10:0] instruction_memory_1_bit11;
  wire [11:0] alucontrol_1_aluctrl;
  wire [15:0] multiplexer_2_out;
  wire [31:0] alu_1_result, data_memory_1_out_6, extendunit_1_out_3, multiplexer_3_out, multiplexer_4_out,
       multiplexer_5_out, multiplexer_6_out, pcunit_1_nextpc32, regfile_1_busa, regfile_1_busb, shifter_1_out;

  PCUnit pcunit_1 (
    .ImmL5(instruction_memory_1_rd_imml), .JALRPC(alu_1_result[19:0]), .Branch(alu_1_branch), .PCSrc(PCSrc),
    .Clock(clock_1_out), .ImmU11(instruction_memory_1_bit11), .NextPC32(pcunit_1_nextpc32), .PC20(out_23));
  Clock clock_1 (.out(clock_1_out));
  ControlUnit controlunit_1 (
    .opcode(instruction_memory_1_opcode), .MemWrite(MemWrite), .MemRead(MemRead), .ALUsrc(ALUsrc),
    .RegW(RegW), .JALR(JALR), .SSET(SSET), .PCSrc(PCSrc), .ZeroExtend(ZeroExtend), .SB(SB),
    .MemtoReg(MemToReg));
  instruction_memory instruction_memory_1 (
    .address(out_23), .opcode(instruction_memory_1_opcode), .RD_IMML(instruction_memory_1_rd_imml),
    .RS1(instruction_memory_1_rs1), .RS2_IMM5(instruction_memory_1_rs2_imm5),
    .bit11(instruction_memory_1_bit11));
  ALUcontrol alucontrol_1 (
    .func(instruction_memory_1_bit11), .OPcode(instruction_memory_1_opcode), .ALUctrl(alucontrol_1_aluctrl));
  Multiplexer #(.width(5)) multiplexer_1 (
    .in0(instruction_memory_1_rs1), .in1(instruction_memory_1_rd_imml), .out(multiplexer_1_out), .sel(SSET));
  Multiplexer #(.width(16)) multiplexer_2 (
    .in0({instruction_memory_1_bit11, instruction_memory_1_rs2_imm5}),
    .in1({instruction_memory_1_bit11, instruction_memory_1_rd_imml}), .out(multiplexer_2_out), .sel(SB));
  ExtendUnit extendunit_1 (.in_2(multiplexer_2_out), .ExtendOp(ZeroExtend), .out_3(extendunit_1_out_3));
  Multiplexer #(.width(32)) multiplexer_3 (
    .in0(multiplexer_6_out), .in1(pcunit_1_nextpc32), .out(multiplexer_3_out), .sel(JALR));
  regFile regfile_1 (
    .RegWrite(RegW), .CLK(clock_1_out), .RA(multiplexer_1_out), .Busw(multiplexer_3_out),
    .RB(instruction_memory_1_rs2_imm5), .RW(instruction_memory_1_rd_imml), .out_12(out_17), .out_13(out_20),
    .out_14(out_24), .out_15(out_27), .out_16(out_30), .out_17(out_2), .out_18(out_6), .out_19(out_10),
    .out_20(out_14), .out_21(out_18), .out_22(out_21), .out_23(out_25), .out_24(out_28), .out_25(out_31),
    .out_26(out_3), .out_27(out_7), .out_28(out_11), .out_29(out_15), .out_30(out_19), .out_31(out_22),
    .out_32(out_26), .out_33(out_29), .out_34(out_32), .out_35(out_4), .out_36(out_8), .out_37(out_12),
    .out_38(out_16), .out_8(out_1), .out_9(out_5), .out_10(out_9), .out_11(out_13), .BusA(regfile_1_busa),
    .BusB(regfile_1_busb));  // open: out_7
  Shifter #(.width(32)) shifter_1 (.in(regfile_1_busa), .\dist (5'b10000), .out(shifter_1_out));
  Multiplexer #(.width(32)) multiplexer_4 (
    .in0(regfile_1_busa), .in1(shifter_1_out), .out(multiplexer_4_out), .sel(SSET));
  ALU alu_1 (
    .ALUctrl(alucontrol_1_aluctrl), .A(multiplexer_4_out), .B(multiplexer_5_out), .Result(alu_1_result),
    .Branch(alu_1_branch));
  Multiplexer #(.width(32)) multiplexer_5 (
    .in0(regfile_1_busb), .in1(extendunit_1_out_3), .out(multiplexer_5_out), .sel(ALUsrc));
  data_memory data_memory_1 (
    .address(alu_1_result[19:0]), .data(regfile_1_busb), .write_enable(MemWrite), .out_enable(MemRead),
    .CLK(clock_1_out), .out_6(data_memory_1_out_6));
  Multiplexer #(.width(32)) multiplexer_6 (
    .in0(alu_1_result), .in1(data_memory_1_out_6), .out(multiplexer_6_out), .sel(MemToReg));

  // Other names for the same wires on the sheet: PC[19:0] = out_23; R1[31:0] = out_1; R2[31:0] = out_5;
  //   R3[31:0] = out_9; R4[31:0] = out_13; R5[31:0] = out_17; R6[31:0] = out_20; R7[31:0] = out_24; R8[31:0] = out_27;
  //   R9[31:0] = out_30; R10[31:0] = out_2; R11[31:0] = out_6; R12[31:0] = out_10; R13[31:0] = out_14;
  //   R14[31:0] = out_18; R15[31:0] = out_21; R16[31:0] = out_25; R17[31:0] = out_28; R18[31:0] = out_31;
  //   R19[31:0] = out_3; R20[31:0] = out_7; R21[31:0] = out_11; R22[31:0] = out_15; R23[31:0] = out_19;
  //   R24[31:0] = out_22; R25[31:0] = out_26; R26[31:0] = out_29; R27[31:0] = out_32; R28[31:0] = out_4;
  //   R29[31:0] = out_8; R30[31:0] = out_12; R31[31:0] = out_16

  // Notes on the sheet:
  //   16bit imm
  //   16bit immU, immL
endmodule

module ALU (
  input  [31:0] A,
  input  [31:0] B,
  input  [11:0] ALUctrl,
  output [31:0] Result,
  output Branch
);

  wire comparator_1_eq, comparator_1_lt, comparator_2_lt, multiplexer_4_out, not_3_out, not_4_out, not_5_out;
  wire [31:0] adder_1_out, and_1_out, bit_extender_1_out, multiplexer_1_out, multiplexer_2_out,
       multiplexer_3_out, multiplier_1_out, not_1_out, not_2_out, or_1_out, shifter_1_out, shifter_2_out,
       shifter_3_out, shifter_4_out, xor_1_out;

  assign not_1_out = ~A;  // NOT_Gate not_1, 32 bits wide
  assign not_2_out = ~B;  // NOT_Gate not_2, 32 bits wide
  Multiplexer #(.width(32)) multiplexer_1 (.in0(A), .in1(not_1_out), .out(multiplexer_1_out), .sel(ALUctrl[0]));
  Multiplexer #(.width(32)) multiplexer_2 (.in0(B), .in1(not_2_out), .out(multiplexer_2_out), .sel(ALUctrl[1]));
  Shifter #(.width(32)) shifter_1 (.in(multiplexer_1_out), .\dist (multiplexer_2_out[4:0]), .out(shifter_1_out));
  Shifter #(.shift("lr"), .width(32)) shifter_2 (
    .in(multiplexer_1_out), .\dist (multiplexer_2_out[4:0]), .out(shifter_2_out));
  Shifter #(.shift("ar"), .width(32)) shifter_3 (
    .in(multiplexer_1_out), .\dist (multiplexer_2_out[4:0]), .out(shifter_3_out));
  Shifter #(.shift("rr"), .width(32)) shifter_4 (
    .in(multiplexer_1_out), .\dist (multiplexer_2_out[4:0]), .out(shifter_4_out));
  assign xor_1_out = multiplexer_1_out ^ multiplexer_2_out;  // XOR_Gate xor_1, 32 bits wide
  assign or_1_out = multiplexer_1_out | multiplexer_2_out;  // OR_Gate or_1, 32 bits wide
  assign and_1_out = multiplexer_1_out & multiplexer_2_out;  // AND_Gate and_1, 32 bits wide
  Multiplier #(.width(32)) multiplier_1 (
    .a(multiplexer_1_out), .b(multiplexer_2_out), .out(multiplier_1_out));  // open: cin, cout
  Adder #(.width(32)) adder_1 (
    .a(multiplexer_1_out), .b(multiplexer_2_out), .out(adder_1_out), .cin(ALUctrl[1]));  // open: cout
  Comparator #(.width(32)) comparator_1 (.a(A), .b(B), .eq(comparator_1_eq), .lt(comparator_1_lt));  // open: gt
  Comparator #(.mode("unsigned"), .width(32)) comparator_2 (.a(A), .b(B), .lt(comparator_2_lt));  // open: gt, eq
  not not_3 (not_3_out, comparator_1_lt);
  not not_4 (not_4_out, comparator_1_eq);
  not not_5 (not_5_out, comparator_2_lt);
  Multiplexer #(.select(2), .width(32)) multiplexer_3 (
    .in0(shifter_1_out), .in1(shifter_2_out), .in2(shifter_3_out), .in3(shifter_4_out),
    .out(multiplexer_3_out), .sel(ALUctrl[3:2]));
  assign bit_extender_1_out = {{31{1'b0}}, multiplexer_4_out};  // Bit_Extender bit_extender_1
  Multiplexer #(.select(2)) multiplexer_4 (
    .in0(comparator_1_eq), .in1(comparator_1_lt), .in2(comparator_2_lt), .out(multiplexer_4_out),
    .sel(ALUctrl[5:4]));  // open: in3
  Multiplexer #(.select(3)) multiplexer_5 (
    .in0(1'b0), .in1(comparator_1_lt), .in2(not_3_out), .in3(comparator_1_eq), .in4(not_4_out),
    .in5(comparator_2_lt), .in6(not_5_out), .out(Branch), .sel(ALUctrl[8:6]));  // open: in7
  Multiplexer #(.select(3), .width(32)) multiplexer_6 (
    .in0(multiplexer_3_out), .in1(adder_1_out), .in2(bit_extender_1_out), .in3(xor_1_out), .in4(or_1_out),
    .in5(and_1_out), .in6(multiplier_1_out), .out(Result), .sel(ALUctrl[11:9]));  // open: in7

  // Other names for the same wires on the sheet: Ainvert = ALUctrl[0]; Binvert = ALUctrl[1];
  //   ShiftOp[1:0] = ALUctrl[3:2]; SetOp[1:0] = ALUctrl[5:4]; BranchOp[2:0] = ALUctrl[8:6];
  //   ALUop[2:0] = ALUctrl[11:9]
endmodule

module PCUnit (
  input  Branch,
  input  [10:0] ImmU11,
  input  [19:0] JALRPC,
  input  Clock,
  input  [4:0] ImmL5,
  input  [1:0] PCSrc,
  output [31:0] NextPC32,
  output [19:0] PC20
);

  wire [1:0] multiplexer_2_out;
  wire [19:0] adder_1_out, adder_2_out, bit_extender_1_out, multiplexer_1_out;

  Multiplexer #(.select(2), .width(20)) multiplexer_1 (
    .in0(adder_1_out), .in1(adder_2_out), .in2(JALRPC), .out(multiplexer_1_out), .sel(multiplexer_2_out));  // open: in3
  Multiplexer #(.width(2)) multiplexer_2 (.in0(PCSrc), .in1(2'b01), .out(multiplexer_2_out), .sel(Branch));
  Register #(.width(20)) ProgramCounter (.D(multiplexer_1_out), .en(1'b1), .clk(Clock), .Q(PC20));  // open: clr
  Adder #(.width(20)) adder_1 (.a(PC20), .b(20'h1), .out(adder_1_out));  // open: cin, cout
  assign bit_extender_1_out = {{4{ImmU11[10]}}, {ImmU11, ImmL5}};  // Bit_Extender bit_extender_1
  Adder #(.width(20)) adder_2 (.a(PC20), .b(bit_extender_1_out), .out(adder_2_out));  // open: cin, cout
  assign NextPC32 = {{12{adder_1_out[19]}}, adder_1_out};  // Bit_Extender bit_extender_2
endmodule

module instruction_memory (
  input  [19:0] address,
  output [5:0] opcode,
  output [4:0] RD_IMML,
  output [4:0] RS1,
  output [4:0] RS2_IMM5,
  output [10:0] bit11
);

  ROM #(.addrWidth(20), .dataWidth(32)) rom_1 (.addr(address), .data({bit11, RS2_IMM5, RS1, RD_IMML, opcode}));

  // Notes on the sheet:
  //   contents of rom_1 (hex, n*v repeats v):
  //   384004d 1234020d 5678020e 140945 12508c0 834100 50 10090 200d0 a42100 841100 c31180 30d2 820880
  //   ffe00712 40011 1a31280 245380 4453c0 57684 1a01cf 4545024d 4545028d 95095 ffff0dcb 12 1431140 50
  //   50890 608d0 1631100 40011 380f
endmodule

module data_memory (
  input  [19:0] address,
  input  [31:0] data,
  input  CLK,
  input  out_enable,
  input  write_enable,
  output [31:0] out_6
);

  RAM #(.addrWidth(20), .dataWidth(32), .trigger("falling")) ram_1 (
    .addr(address), .we(write_enable), .oe(out_enable), .clk(CLK), .din(data), .dout(out_6));
endmodule

module ControlUnit (
  input  [5:0] opcode,
  output MemtoReg,
  output MemWrite,
  output MemRead,
  output ALUsrc,
  output RegW,
  output JALR,
  output SSET,
  output [1:0] PCSrc,
  output ZeroExtend,
  output SB
);

  wire and_3_out, and_4_out, and_5_out, and_6_out, and_10_out, and_11_out, and_12_out, and_13_out,
       and_14_out, and_15_out, and_16_out, not_1_out, not_2_out, not_3_out, not_4_out, not_5_out;

  not not_1 (not_1_out, opcode[4]);
  not not_2 (not_2_out, opcode[3]);
  not not_3 (not_3_out, opcode[2]);
  not not_4 (not_4_out, opcode[1]);
  not not_5 (not_5_out, opcode[0]);
  and and_1 (MemWrite, opcode[4], not_3_out, not_4_out, opcode[0]);
  and and_2 (MemRead, opcode[4], not_3_out, not_4_out, not_5_out);
  and and_3 (and_3_out, not_1_out, opcode[2], opcode[0]);
  and and_4 (and_4_out, not_1_out, opcode[2], opcode[1]);
  and and_5 (and_5_out, opcode[4], not_3_out, not_4_out);
  and and_6 (and_6_out, not_3_out, not_4_out, not_5_out);
  and and_7 (JALR, opcode[3], opcode[2], opcode[1], opcode[0]);
  and and_8 (SSET, opcode[3], opcode[2], opcode[1], not_5_out);
  and and_9 (PCSrc[1], opcode[3], opcode[2], opcode[1], opcode[0]);
  and and_10 (and_10_out, not_1_out, not_2_out, opcode[1], opcode[0]);
  and and_11 (and_11_out, opcode[3], opcode[2], not_5_out);
  and and_12 (and_12_out, not_1_out, not_3_out, opcode[0]);
  and and_13 (and_13_out, not_1_out, not_3_out, opcode[1]);
  and and_14 (and_14_out, opcode[4], opcode[0]);
  and and_15 (and_15_out, opcode[4], opcode[1]);
  and and_16 (and_16_out, opcode[4], opcode[2]);
  or or_1 (ALUsrc, and_3_out, and_4_out, opcode[3], and_5_out);
  or or_2 (RegW, not_1_out, and_6_out);
  or or_3 (ZeroExtend, and_10_out, and_11_out, and_12_out, and_13_out);
  or or_4 (SB, and_14_out, and_15_out, and_16_out);

  assign MemtoReg = opcode[4];
  assign PCSrc[0] = 1'b0;
endmodule

module ExtendUnit (
  input  ExtendOp,
  input  [15:0] in_2,
  output [31:0] out_3
);

  wire [31:0] bit_extender_1_out, bit_extender_2_out;

  assign bit_extender_1_out = {{16{in_2[15]}}, in_2};  // Bit_Extender bit_extender_1
  Multiplexer #(.width(32)) multiplexer_1 (
    .in0(bit_extender_1_out), .in1(bit_extender_2_out), .out(out_3), .sel(ExtendOp));
  assign bit_extender_2_out = {{16{1'b0}}, in_2};  // Bit_Extender bit_extender_2
endmodule

module ALUcontrol (
  input  [10:0] func,
  input  [5:0] OPcode,
  output [11:0] ALUctrl
);

  wire and_2_out, and_3_out, and_4_out, and_5_out, and_6_out, and_7_out, and_8_out, and_9_out, and_10_out,
       and_11_out, and_14_out, and_15_out, and_16_out, and_17_out, and_18_out, and_19_out, and_20_out,
       and_21_out, and_22_out, and_23_out, and_24_out, and_25_out, and_26_out, and_27_out, not_2_out,
       not_3_out, not_4_out, not_6_out, not_7_out, S;
  wire [11:0] FuncOut, OpCodeOut;

  not not_1 (FuncOut[4], func[3]);
  not not_2 (not_2_out, func[2]);
  not not_3 (not_3_out, func[1]);
  not not_4 (not_4_out, func[0]);
  and and_1 (FuncOut[0], func[3], func[2], not_4_out);
  and and_2 (and_2_out, FuncOut[4], func[2], not_3_out, func[0]);
  and and_3 (and_3_out, func[3], func[2], not_4_out);
  and and_4 (and_4_out, func[3], func[1]);
  and and_5 (and_5_out, func[3], func[2]);
  and and_6 (and_6_out, func[2], func[1]);
  and and_7 (and_7_out, func[3], not_2_out, not_3_out);
  and and_8 (and_8_out, func[3], not_3_out, func[0]);
  and and_9 (and_9_out, FuncOut[4], func[2], not_3_out);
  and and_10 (and_10_out, func[3], not_2_out, func[0]);
  and and_11 (and_11_out, func[2], not_3_out, not_4_out);
  or or_1 (FuncOut[1], and_2_out, and_3_out);
  or or_2 (FuncOut[11], and_4_out, and_5_out);
  or or_3 (FuncOut[10], and_6_out, and_7_out, and_8_out);
  or or_4 (FuncOut[9], and_9_out, and_10_out, and_11_out);
  or or_5 (S, OPcode[0], OPcode[1], OPcode[2], OPcode[3], OPcode[4], OPcode[5]);
  not not_5 (OpCodeOut[4], OPcode[3]);
  not not_6 (not_6_out, OPcode[2]);
  not not_7 (not_7_out, OPcode[1]);
  not not_8 (OpCodeOut[2], OPcode[0]);
  Multiplexer #(.width(12)) multiplexer_1 (
    .in0({FuncOut[11:9], 3'b000, func[0], FuncOut[4], func[1:0], FuncOut[1:0]}),
    .in1({OpCodeOut[11:6], OPcode[0], OpCodeOut[4:0]}), .out(ALUctrl), .sel(S));
  and and_12 (OpCodeOut[0], OPcode[3], OPcode[2], not_7_out, OpCodeOut[2]);
  and and_13 (OpCodeOut[1], OPcode[3], OPcode[2], not_7_out, OpCodeOut[2]);
  and and_14 (and_14_out, OPcode[1], OPcode[0]);
  and and_15 (and_15_out, OPcode[4], OPcode[1], OPcode[0]);
  and and_16 (and_16_out, OPcode[4], OPcode[2], OPcode[1]);
  and and_17 (and_17_out, OPcode[4], not_6_out, OPcode[1], OpCodeOut[2]);
  and and_18 (and_18_out, OPcode[4], OPcode[2], OPcode[0]);
  and and_19 (and_19_out, OPcode[4], OPcode[1], OpCodeOut[2]);
  and and_20 (and_20_out, OPcode[4], OPcode[2], OpCodeOut[2]);
  and and_21 (and_21_out, OPcode[3], not_6_out, OPcode[1]);
  and and_22 (and_22_out, OPcode[3], OPcode[2], not_7_out, OpCodeOut[2]);
  and and_23 (and_23_out, OpCodeOut[4], OPcode[2], OPcode[1]);
  and and_24 (and_24_out, OPcode[3], not_6_out, not_7_out);
  and and_25 (and_25_out, OPcode[2], not_7_out, OPcode[0]);
  and and_26 (and_26_out, OPcode[3], OPcode[0]);
  and and_27 (and_27_out, OPcode[3], OPcode[2]);
  or or_6 (OpCodeOut[3], and_14_out, OPcode[2]);
  or or_7 (OpCodeOut[8], and_15_out, and_16_out);
  or or_8 (OpCodeOut[7], and_17_out, and_18_out);
  or or_9 (OpCodeOut[6], and_19_out, and_20_out);
  or or_10 (OpCodeOut[11], and_21_out, and_22_out);
  or or_11 (OpCodeOut[10], and_23_out, and_24_out);
  or or_12 (OpCodeOut[9], and_25_out, and_26_out, and_27_out, OPcode[4]);

  // Other names for the same wires on the sheet: FuncOut (some bits) = {func[0], func[1:0]}; OpCodeOut[5] = OPcode[0]
endmodule

module regFile (
  input  [4:0] RB,
  input  [4:0] RA,
  input  [4:0] RW,
  input  RegWrite,
  input  [31:0] Busw,
  input  CLK,
  output [31:0] out_7,
  output [31:0] out_8,
  output [31:0] out_9,
  output [31:0] out_10,
  output [31:0] out_11,
  output [31:0] out_12,
  output [31:0] out_13,
  output [31:0] out_14,
  output [31:0] out_15,
  output [31:0] out_16,
  output [31:0] out_17,
  output [31:0] out_18,
  output [31:0] out_19,
  output [31:0] out_20,
  output [31:0] out_21,
  output [31:0] out_22,
  output [31:0] out_23,
  output [31:0] out_24,
  output [31:0] out_25,
  output [31:0] out_26,
  output [31:0] out_27,
  output [31:0] out_28,
  output [31:0] out_29,
  output [31:0] out_30,
  output [31:0] out_31,
  output [31:0] out_32,
  output [31:0] out_33,
  output [31:0] out_34,
  output [31:0] out_35,
  output [31:0] out_36,
  output [31:0] out_37,
  output [31:0] out_38,
  output [31:0] BusB,
  output [31:0] BusA
);

  wire and_1_out, and_2_out, and_3_out, and_4_out, and_5_out, and_6_out, and_7_out, and_8_out, and_9_out,
       and_10_out, and_11_out, and_12_out, and_13_out, and_14_out, and_15_out, and_16_out, and_17_out,
       and_18_out, and_19_out, and_20_out, and_21_out, and_22_out, and_23_out, and_24_out, and_25_out,
       and_26_out, and_27_out, and_28_out, and_29_out, and_30_out, and_31_out, decoder_1_out1,
       decoder_1_out2, decoder_1_out3, decoder_1_out4, decoder_1_out5, decoder_1_out6, decoder_1_out7,
       decoder_1_out8, decoder_1_out9, decoder_1_out10, decoder_1_out11, decoder_1_out12, decoder_1_out13,
       decoder_1_out14, decoder_1_out15, decoder_1_out16, decoder_1_out17, decoder_1_out18, decoder_1_out19,
       decoder_1_out20, decoder_1_out21, decoder_1_out22, decoder_1_out23, decoder_1_out24, decoder_1_out25,
       decoder_1_out26, decoder_1_out27, decoder_1_out28, decoder_1_out29, decoder_1_out30, decoder_1_out31,
       decoder_2_out0, decoder_2_out1, decoder_2_out2, decoder_2_out3, decoder_2_out4, decoder_2_out5,
       decoder_2_out6, decoder_2_out7, decoder_2_out8, decoder_2_out9, decoder_2_out10, decoder_2_out11,
       decoder_2_out12, decoder_2_out13, decoder_2_out14, decoder_2_out15, decoder_2_out16, decoder_2_out17,
       decoder_2_out18, decoder_2_out19, decoder_2_out20, decoder_2_out21, decoder_2_out22, decoder_2_out23,
       decoder_2_out24, decoder_2_out25, decoder_2_out26, decoder_2_out27, decoder_2_out28, decoder_2_out29,
       decoder_2_out30, decoder_2_out31, decoder_3_out0, decoder_3_out1, decoder_3_out2, decoder_3_out3,
       decoder_3_out4, decoder_3_out5, decoder_3_out6, decoder_3_out7, decoder_3_out8, decoder_3_out9,
       decoder_3_out10, decoder_3_out11, decoder_3_out12, decoder_3_out13, decoder_3_out14, decoder_3_out15,
       decoder_3_out16, decoder_3_out17, decoder_3_out18, decoder_3_out19, decoder_3_out20, decoder_3_out21,
       decoder_3_out22, decoder_3_out23, decoder_3_out24, decoder_3_out25, decoder_3_out26, decoder_3_out27,
       decoder_3_out28, decoder_3_out29, decoder_3_out30, decoder_3_out31;

  Decoder #(.enable("false"), .select(5)) decoder_1 (
    .out1(decoder_1_out1), .out2(decoder_1_out2), .out3(decoder_1_out3), .out4(decoder_1_out4),
    .out5(decoder_1_out5), .out6(decoder_1_out6), .out7(decoder_1_out7), .out8(decoder_1_out8),
    .out9(decoder_1_out9), .out10(decoder_1_out10), .out11(decoder_1_out11), .out12(decoder_1_out12),
    .out13(decoder_1_out13), .out14(decoder_1_out14), .out15(decoder_1_out15), .out16(decoder_1_out16),
    .out17(decoder_1_out17), .out18(decoder_1_out18), .out19(decoder_1_out19), .out20(decoder_1_out20),
    .out21(decoder_1_out21), .out22(decoder_1_out22), .out23(decoder_1_out23), .out24(decoder_1_out24),
    .out25(decoder_1_out25), .out26(decoder_1_out26), .out27(decoder_1_out27), .out28(decoder_1_out28),
    .out29(decoder_1_out29), .out30(decoder_1_out30), .out31(decoder_1_out31), .sel(RW));  // open: out0
  Register #(.width(32)) register_1 (.D(Busw), .en(and_1_out), .clk(CLK), .Q(out_8));  // open: clr
  and and_1 (and_1_out, decoder_1_out1, RegWrite);
  Register #(.width(32)) register_2 (.D(Busw), .en(and_2_out), .clk(CLK), .Q(out_9));  // open: clr
  and and_2 (and_2_out, decoder_1_out2, RegWrite);
  Register #(.width(32)) register_3 (.D(Busw), .en(and_3_out), .clk(CLK), .Q(out_10));  // open: clr
  and and_3 (and_3_out, decoder_1_out3, RegWrite);
  Register #(.width(32)) register_4 (.D(Busw), .en(and_4_out), .clk(CLK), .Q(out_11));  // open: clr
  and and_4 (and_4_out, decoder_1_out4, RegWrite);
  Register #(.width(32)) register_5 (.D(Busw), .en(and_5_out), .clk(CLK), .Q(out_12));  // open: clr
  and and_5 (and_5_out, decoder_1_out5, RegWrite);
  Register #(.width(32)) register_6 (.D(Busw), .en(and_6_out), .clk(CLK), .Q(out_13));  // open: clr
  and and_6 (and_6_out, decoder_1_out6, RegWrite);
  Register #(.width(32)) register_7 (.D(Busw), .en(and_7_out), .clk(CLK), .Q(out_14));  // open: clr
  and and_7 (and_7_out, decoder_1_out7, RegWrite);
  Register #(.width(32)) register_8 (.D(Busw), .en(and_8_out), .clk(CLK), .Q(out_15));  // open: clr
  and and_8 (and_8_out, decoder_1_out8, RegWrite);
  Register #(.width(32)) register_9 (.D(Busw), .en(and_9_out), .clk(CLK), .Q(out_16));  // open: clr
  and and_9 (and_9_out, decoder_1_out9, RegWrite);
  Register #(.width(32)) register_10 (.D(Busw), .en(and_10_out), .clk(CLK), .Q(out_17));  // open: clr
  and and_10 (and_10_out, decoder_1_out10, RegWrite);
  Register #(.width(32)) register_11 (.D(Busw), .en(and_11_out), .clk(CLK), .Q(out_18));  // open: clr
  and and_11 (and_11_out, decoder_1_out11, RegWrite);
  Register #(.width(32)) register_12 (.D(Busw), .en(and_12_out), .clk(CLK), .Q(out_19));  // open: clr
  and and_12 (and_12_out, decoder_1_out12, RegWrite);
  Register #(.width(32)) register_13 (.D(Busw), .en(and_13_out), .clk(CLK), .Q(out_20));  // open: clr
  and and_13 (and_13_out, decoder_1_out13, RegWrite);
  Register #(.width(32)) register_14 (.D(Busw), .en(and_14_out), .clk(CLK), .Q(out_21));  // open: clr
  and and_14 (and_14_out, decoder_1_out14, RegWrite);
  Register #(.width(32)) register_15 (.D(Busw), .en(and_15_out), .clk(CLK), .Q(out_22));  // open: clr
  and and_15 (and_15_out, decoder_1_out15, RegWrite);
  Register #(.width(32)) register_16 (.D(Busw), .en(and_16_out), .clk(CLK), .Q(out_23));  // open: clr
  and and_16 (and_16_out, decoder_1_out16, RegWrite);
  Register #(.width(32)) register_17 (.D(Busw), .en(and_17_out), .clk(CLK), .Q(out_24));  // open: clr
  and and_17 (and_17_out, decoder_1_out17, RegWrite);
  Register #(.width(32)) register_18 (.D(Busw), .en(and_18_out), .clk(CLK), .Q(out_25));  // open: clr
  and and_18 (and_18_out, decoder_1_out18, RegWrite);
  Register #(.width(32)) register_19 (.D(Busw), .en(and_19_out), .clk(CLK), .Q(out_26));  // open: clr
  and and_19 (and_19_out, decoder_1_out19, RegWrite);
  Register #(.width(32)) register_20 (.D(Busw), .en(and_20_out), .clk(CLK), .Q(out_27));  // open: clr
  and and_20 (and_20_out, decoder_1_out20, RegWrite);
  Register #(.width(32)) register_21 (.D(Busw), .en(and_21_out), .clk(CLK), .Q(out_28));  // open: clr
  and and_21 (and_21_out, decoder_1_out21, RegWrite);
  Register #(.width(32)) register_22 (.D(Busw), .en(and_22_out), .clk(CLK), .Q(out_29));  // open: clr
  and and_22 (and_22_out, decoder_1_out22, RegWrite);
  Register #(.width(32)) register_23 (.D(Busw), .en(and_23_out), .clk(CLK), .Q(out_30));  // open: clr
  and and_23 (and_23_out, decoder_1_out23, RegWrite);
  Register #(.width(32)) register_24 (.D(Busw), .en(and_24_out), .clk(CLK), .Q(out_31));  // open: clr
  and and_24 (and_24_out, decoder_1_out24, RegWrite);
  Register #(.width(32)) register_25 (.D(Busw), .en(and_25_out), .clk(CLK), .Q(out_32));  // open: clr
  and and_25 (and_25_out, decoder_1_out25, RegWrite);
  Register #(.width(32)) register_26 (.D(Busw), .en(and_26_out), .clk(CLK), .Q(out_33));  // open: clr
  and and_26 (and_26_out, decoder_1_out26, RegWrite);
  Register #(.width(32)) register_27 (.D(Busw), .en(and_27_out), .clk(CLK), .Q(out_34));  // open: clr
  and and_27 (and_27_out, decoder_1_out27, RegWrite);
  Register #(.width(32)) register_28 (.D(Busw), .en(and_28_out), .clk(CLK), .Q(out_35));  // open: clr
  and and_28 (and_28_out, decoder_1_out28, RegWrite);
  Register #(.width(32)) register_29 (.D(Busw), .en(and_29_out), .clk(CLK), .Q(out_36));  // open: clr
  and and_29 (and_29_out, decoder_1_out29, RegWrite);
  Register #(.width(32)) register_30 (.D(Busw), .en(and_30_out), .clk(CLK), .Q(out_37));  // open: clr
  and and_30 (and_30_out, decoder_1_out30, RegWrite);
  Register #(.width(32)) register_31 (.D(Busw), .en(and_31_out), .clk(CLK), .Q(out_38));  // open: clr
  and and_31 (and_31_out, decoder_1_out31, RegWrite);
  Decoder #(.enable("false"), .select(5)) decoder_2 (
    .out0(decoder_2_out0), .out1(decoder_2_out1), .out2(decoder_2_out2), .out3(decoder_2_out3),
    .out4(decoder_2_out4), .out5(decoder_2_out5), .out6(decoder_2_out6), .out7(decoder_2_out7),
    .out8(decoder_2_out8), .out9(decoder_2_out9), .out10(decoder_2_out10), .out11(decoder_2_out11),
    .out12(decoder_2_out12), .out13(decoder_2_out13), .out14(decoder_2_out14), .out15(decoder_2_out15),
    .out16(decoder_2_out16), .out17(decoder_2_out17), .out18(decoder_2_out18), .out19(decoder_2_out19),
    .out20(decoder_2_out20), .out21(decoder_2_out21), .out22(decoder_2_out22), .out23(decoder_2_out23),
    .out24(decoder_2_out24), .out25(decoder_2_out25), .out26(decoder_2_out26), .out27(decoder_2_out27),
    .out28(decoder_2_out28), .out29(decoder_2_out29), .out30(decoder_2_out30), .out31(decoder_2_out31),
    .sel(RA));
  assign BusA = decoder_2_out2 ? out_9 : 32'bz;  // Controlled_Buffer controlled_buffer_1
  assign BusA = decoder_2_out3 ? out_10 : 32'bz;  // Controlled_Buffer controlled_buffer_2
  assign BusA = decoder_2_out4 ? out_11 : 32'bz;  // Controlled_Buffer controlled_buffer_3
  assign BusA = decoder_2_out5 ? out_12 : 32'bz;  // Controlled_Buffer controlled_buffer_4
  assign BusA = decoder_2_out6 ? out_13 : 32'bz;  // Controlled_Buffer controlled_buffer_5
  assign BusA = decoder_2_out7 ? out_14 : 32'bz;  // Controlled_Buffer controlled_buffer_6
  assign BusA = decoder_2_out8 ? out_15 : 32'bz;  // Controlled_Buffer controlled_buffer_7
  assign BusA = decoder_2_out9 ? out_16 : 32'bz;  // Controlled_Buffer controlled_buffer_8
  assign BusA = decoder_2_out10 ? out_17 : 32'bz;  // Controlled_Buffer controlled_buffer_9
  assign BusA = decoder_2_out11 ? out_18 : 32'bz;  // Controlled_Buffer controlled_buffer_10
  assign BusA = decoder_2_out12 ? out_19 : 32'bz;  // Controlled_Buffer controlled_buffer_11
  assign BusA = decoder_2_out13 ? out_20 : 32'bz;  // Controlled_Buffer controlled_buffer_12
  assign BusA = decoder_2_out14 ? out_21 : 32'bz;  // Controlled_Buffer controlled_buffer_13
  assign BusA = decoder_2_out15 ? out_22 : 32'bz;  // Controlled_Buffer controlled_buffer_14
  assign BusA = decoder_2_out16 ? out_23 : 32'bz;  // Controlled_Buffer controlled_buffer_15
  assign BusA = decoder_2_out17 ? out_24 : 32'bz;  // Controlled_Buffer controlled_buffer_16
  assign BusA = decoder_2_out18 ? out_25 : 32'bz;  // Controlled_Buffer controlled_buffer_17
  assign BusA = decoder_2_out19 ? out_26 : 32'bz;  // Controlled_Buffer controlled_buffer_18
  assign BusA = decoder_2_out20 ? out_27 : 32'bz;  // Controlled_Buffer controlled_buffer_19
  assign BusA = decoder_2_out21 ? out_28 : 32'bz;  // Controlled_Buffer controlled_buffer_20
  assign BusA = decoder_2_out22 ? out_29 : 32'bz;  // Controlled_Buffer controlled_buffer_21
  assign BusA = decoder_2_out23 ? out_30 : 32'bz;  // Controlled_Buffer controlled_buffer_22
  assign BusA = decoder_2_out24 ? out_31 : 32'bz;  // Controlled_Buffer controlled_buffer_23
  assign BusA = decoder_2_out25 ? out_32 : 32'bz;  // Controlled_Buffer controlled_buffer_24
  assign BusA = decoder_2_out26 ? out_33 : 32'bz;  // Controlled_Buffer controlled_buffer_25
  assign BusA = decoder_2_out27 ? out_34 : 32'bz;  // Controlled_Buffer controlled_buffer_26
  assign BusA = decoder_2_out28 ? out_35 : 32'bz;  // Controlled_Buffer controlled_buffer_27
  assign BusA = decoder_2_out29 ? out_36 : 32'bz;  // Controlled_Buffer controlled_buffer_28
  assign BusA = decoder_2_out30 ? out_37 : 32'bz;  // Controlled_Buffer controlled_buffer_29
  assign BusA = decoder_2_out31 ? out_38 : 32'bz;  // Controlled_Buffer controlled_buffer_30
  assign BusA = decoder_2_out0 ? {32{1'b0}} : 32'bz;  // Controlled_Buffer controlled_buffer_31
  assign BusA = decoder_2_out1 ? out_8 : 32'bz;  // Controlled_Buffer controlled_buffer_32
  Decoder #(.enable("false"), .select(5)) decoder_3 (
    .out0(decoder_3_out0), .out1(decoder_3_out1), .out2(decoder_3_out2), .out3(decoder_3_out3),
    .out4(decoder_3_out4), .out5(decoder_3_out5), .out6(decoder_3_out6), .out7(decoder_3_out7),
    .out8(decoder_3_out8), .out9(decoder_3_out9), .out10(decoder_3_out10), .out11(decoder_3_out11),
    .out12(decoder_3_out12), .out13(decoder_3_out13), .out14(decoder_3_out14), .out15(decoder_3_out15),
    .out16(decoder_3_out16), .out17(decoder_3_out17), .out18(decoder_3_out18), .out19(decoder_3_out19),
    .out20(decoder_3_out20), .out21(decoder_3_out21), .out22(decoder_3_out22), .out23(decoder_3_out23),
    .out24(decoder_3_out24), .out25(decoder_3_out25), .out26(decoder_3_out26), .out27(decoder_3_out27),
    .out28(decoder_3_out28), .out29(decoder_3_out29), .out30(decoder_3_out30), .out31(decoder_3_out31),
    .sel(RB));
  assign BusB = decoder_3_out0 ? {32{1'b0}} : 32'bz;  // Controlled_Buffer controlled_buffer_33
  assign BusB = decoder_3_out1 ? out_8 : 32'bz;  // Controlled_Buffer controlled_buffer_34
  assign BusB = decoder_3_out2 ? out_9 : 32'bz;  // Controlled_Buffer controlled_buffer_35
  assign BusB = decoder_3_out3 ? out_10 : 32'bz;  // Controlled_Buffer controlled_buffer_36
  assign BusB = decoder_3_out4 ? out_11 : 32'bz;  // Controlled_Buffer controlled_buffer_37
  assign BusB = decoder_3_out5 ? out_12 : 32'bz;  // Controlled_Buffer controlled_buffer_38
  assign BusB = decoder_3_out6 ? out_13 : 32'bz;  // Controlled_Buffer controlled_buffer_39
  assign BusB = decoder_3_out7 ? out_14 : 32'bz;  // Controlled_Buffer controlled_buffer_40
  assign BusB = decoder_3_out8 ? out_15 : 32'bz;  // Controlled_Buffer controlled_buffer_41
  assign BusB = decoder_3_out9 ? out_16 : 32'bz;  // Controlled_Buffer controlled_buffer_42
  assign BusB = decoder_3_out10 ? out_17 : 32'bz;  // Controlled_Buffer controlled_buffer_43
  assign BusB = decoder_3_out11 ? out_18 : 32'bz;  // Controlled_Buffer controlled_buffer_44
  assign BusB = decoder_3_out12 ? out_19 : 32'bz;  // Controlled_Buffer controlled_buffer_45
  assign BusB = decoder_3_out13 ? out_20 : 32'bz;  // Controlled_Buffer controlled_buffer_46
  assign BusB = decoder_3_out14 ? out_21 : 32'bz;  // Controlled_Buffer controlled_buffer_47
  assign BusB = decoder_3_out15 ? out_22 : 32'bz;  // Controlled_Buffer controlled_buffer_48
  assign BusB = decoder_3_out16 ? out_23 : 32'bz;  // Controlled_Buffer controlled_buffer_49
  assign BusB = decoder_3_out17 ? out_24 : 32'bz;  // Controlled_Buffer controlled_buffer_50
  assign BusB = decoder_3_out18 ? out_25 : 32'bz;  // Controlled_Buffer controlled_buffer_51
  assign BusB = decoder_3_out19 ? out_26 : 32'bz;  // Controlled_Buffer controlled_buffer_52
  assign BusB = decoder_3_out20 ? out_27 : 32'bz;  // Controlled_Buffer controlled_buffer_53
  assign BusB = decoder_3_out21 ? out_28 : 32'bz;  // Controlled_Buffer controlled_buffer_54
  assign BusB = decoder_3_out22 ? out_29 : 32'bz;  // Controlled_Buffer controlled_buffer_55
  assign BusB = decoder_3_out23 ? out_30 : 32'bz;  // Controlled_Buffer controlled_buffer_56
  assign BusB = decoder_3_out24 ? out_31 : 32'bz;  // Controlled_Buffer controlled_buffer_57
  assign BusB = decoder_3_out25 ? out_32 : 32'bz;  // Controlled_Buffer controlled_buffer_58
  assign BusB = decoder_3_out26 ? out_33 : 32'bz;  // Controlled_Buffer controlled_buffer_59
  assign BusB = decoder_3_out27 ? out_34 : 32'bz;  // Controlled_Buffer controlled_buffer_60
  assign BusB = decoder_3_out28 ? out_35 : 32'bz;  // Controlled_Buffer controlled_buffer_61
  assign BusB = decoder_3_out29 ? out_36 : 32'bz;  // Controlled_Buffer controlled_buffer_62
  assign BusB = decoder_3_out30 ? out_37 : 32'bz;  // Controlled_Buffer controlled_buffer_63
  assign BusB = decoder_3_out31 ? out_38 : 32'bz;  // Controlled_Buffer controlled_buffer_64

  assign out_7 = {32{1'b0}};

  // Other names for the same wires on the sheet: R1[31:0] = out_8; R2[31:0] = out_9; R3[31:0] = out_10;
  //   R4[31:0] = out_11; R5[31:0] = out_12; R6[31:0] = out_13; R7[31:0] = out_14; R8[31:0] = out_15;
  //   R9[31:0] = out_16; R10[31:0] = out_17; R11[31:0] = out_18; R12[31:0] = out_19; R13[31:0] = out_20;
  //   R14[31:0] = out_21; R15[31:0] = out_22; R16[31:0] = out_23; R17[31:0] = out_24; R18[31:0] = out_25;
  //   R19[31:0] = out_26; R20[31:0] = out_27; R21[31:0] = out_28; R22[31:0] = out_29; R23[31:0] = out_30;
  //   R24[31:0] = out_31; R25[31:0] = out_32; R26[31:0] = out_33; R27[31:0] = out_34; R28[31:0] = out_35;
  //   R29[31:0] = out_36; R30[31:0] = out_37; R31[31:0] = out_38
endmodule
